// Logisim project Milestone1.circ as structural Verilog: 1 circuit, main circuit main
module main (
);

  wire Clk_out;
  wire [6:0] Address_Register__AR_q, bit_extender_1_out;
  wire [15:0] Accumulator__AC_q, adder_1_out, adder_2_out, AND_out, bit_extender_2_out, Data_Register__DR_q,
       multiplexer_1_out, multiplexer_2_out, OR_out, ram_1_data, subtractor_1_out, Temporary_Register__TR_q,
       XOR_out;

  Bit_Extender #(.in_width(16), .out_width(7)) bit_extender_1 (.in(multiplexer_2_out), .out(bit_extender_1_out));
  Adder #(.width(16)) adder_1 (.a(Data_Register__DR_q), .b(Accumulator__AC_q), .out(adder_1_out));  // open: cin, cout
  Subtractor #(.width(16)) subtractor_1 (
    .a(Data_Register__DR_q), .b(Accumulator__AC_q), .out(subtractor_1_out));  // open: bin, bout
  assign AND_out = Data_Register__DR_q & Accumulator__AC_q;  // AND_Gate AND, 16 bits wide
  assign OR_out = Data_Register__DR_q | Accumulator__AC_q;  // OR_Gate OR, 16 bits wide
  assign XOR_out = Data_Register__DR_q ^ Accumulator__AC_q;  // XOR_Gate XOR, 16 bits wide
  Adder #(.width(16)) adder_2 (.a(Data_Register__DR_q), .b(16'h1), .out(adder_2_out));  // open: cin, cout
  Multiplexer #(.select(3), .width(16)) multiplexer_1 (
    .in1(adder_1_out), .in2(subtractor_1_out), .in3(Data_Register__DR_q), .in4(AND_out), .in5(OR_out),
    .in6(XOR_out), .in7(adder_2_out), .out(multiplexer_1_out), .sel(3'b001));  // open: in0, en
  Register #(.width(7)) Address_Register__AR (
    .D(bit_extender_1_out), .en(1'b0), .Q(Address_Register__AR_q), .clk(Clk_out));  // open: clr
  Register #(.width(16)) Data_Register__DR (
    .D(multiplexer_2_out), .en(1'b0), .Q(Data_Register__DR_q), .clk(Clk_out));  // open: clr
  Register #(.width(16)) Accumulator__AC (
    .D(multiplexer_1_out), .en(1'b1), .Q(Accumulator__AC_q), .clk(Clk_out));  // open: clr
  Register #(.width(16)) Temporary_Register__TR (
    .D(multiplexer_2_out), .en(1'b0), .Q(Temporary_Register__TR_q), .clk(Clk_out));  // open: clr
  RAM #(.addrWidth(7), .dataWidth(16), .bus("separate")) ram_1 (
    .addr(Address_Register__AR_q), .din(multiplexer_2_out), .data(ram_1_data), .str(1'b0), .clk(Clk_out),
    .ld(1'b0));  // open: sel, clr
  assign bit_extender_2_out = {{9{1'b0}}, Address_Register__AR_q};  // Bit_Extender bit_extender_2
  Multiplexer #(.select(3), .width(16)) multiplexer_2 (
    .in0(ram_1_data), .in1(bit_extender_2_out), .in2(Temporary_Register__TR_q), .in3(Data_Register__DR_q),
    .in4(Accumulator__AC_q), .out(multiplexer_2_out), .sel(3'b010));  // open: in5, in6, in7, en
  Clock Clk (.out(Clk_out));
endmodule
