// Logisim project Last updated Milestone 2 co.circ as structural Verilog: 3 circuits, main circuit ALU
module main (
  input  in_1,
  output out_2,
  output out_3
);

  wire AC_Ld, AR_Ld, Clk, DR_Ld, IR_Ld, Memory_Read_En, Memory_Write_En, PC_Inc, PC_Ld, undriven;
  wire [2:0] ALU_Selection_Lines, Bus_Selection_Lines;
  wire [6:0] AR_q, bit_extender_1_out;
  wire [15:0] AC, alu_1_ac_output, bit_extender_2_out, DR_q, IR, multiplexer_1_out, PC_q, ram_1_data, TR_q;

  Bit_Extender #(.in_width(16), .out_width(7)) bit_extender_1 (.in(multiplexer_1_out), .out(bit_extender_1_out));
  Register #(.width(7)) AR (.D(bit_extender_1_out), .en(AR_Ld), .Q(AR_q), .clk(Clk), .clr(1'b0));
  Register #(.width(16)) TR (.D(multiplexer_1_out), .en(undriven), .Q(TR_q), .clk(Clk), .clr(1'b0));
  Register #(.width(16)) DR (.D(multiplexer_1_out), .en(DR_Ld), .Q(DR_q), .clk(Clk), .clr(1'b0));
  Register #(.width(16)) u_AC (.D(alu_1_ac_output), .en(AC_Ld), .Q(AC), .clk(Clk), .clr(1'b0));
  Counter #(.width(16), .max('hffff)) PC (
    .load(PC_Ld), .D(multiplexer_1_out), .count(PC_Inc), .Q(PC_q), .carry(out_3), .clk(Clk), .clr(1'b0));
  Register #(.width(16)) u_IR (.D(multiplexer_1_out), .en(IR_Ld), .Q(IR), .clk(Clk), .clr(1'b0));
  RAM #(.addrWidth(7), .dataWidth(16), .bus("separate")) ram_1 (
    .addr(AR_q), .din(multiplexer_1_out), .data(ram_1_data), .str(Memory_Write_En), .sel(1'b1), .clk(Clk),
    .ld(Memory_Read_En), .clr(1'b0));
  assign bit_extender_2_out = {{9{1'b0}}, AR_q};  // Bit_Extender bit_extender_2
  ALU alu_1 (.A(DR_q), .B(AC), .ALU_Selection_Lines(ALU_Selection_Lines), .E(out_2), .AC_Output(alu_1_ac_output));
  Multiplexer #(.select(3), .width(16)) multiplexer_1 (
    .in0(ram_1_data), .in1(bit_extender_2_out), .in2(TR_q), .in3(DR_q), .in4(AC), .in5(PC_q), .in6(IR),
    .in7({16{1'b0}}), .out(multiplexer_1_out), .sel(Bus_Selection_Lines));  // open: en
  control_unit control_unit_1 (
    .AC(AC), .IR(IR), .Clk(Clk), .AR_Ld(AR_Ld), .DR_Ld(DR_Ld), .AC_Ld(AC_Ld), .PC_Inc(PC_Inc), .PC_Ld(PC_Ld),
    .IR_Ld(IR_Ld), .Memory_Read_En(Memory_Read_En), .Memory_Write_En(Memory_Write_En),
    .Bus_Selection_Lines(Bus_Selection_Lines), .ALU_Selection_Lines(ALU_Selection_Lines));
endmodule

module ALU (
  input  [15:0] A,
  input  [15:0] B,
  input  [2:0] ALU_Selection_Lines,
  output E,
  output [15:0] AC_Output
);

  wire adder_1_cout, adder_2_cout, subtractor_1_bout;
  wire [15:0] adder_1_out, adder_2_out, and_1_out, or_1_out, subtractor_1_out, xor_1_out;

  Adder #(.width(16)) adder_1 (.a(A), .b(B), .out(adder_1_out), .cin(1'b0), .cout(adder_1_cout));
  Subtractor #(.width(16)) subtractor_1 (.a(A), .b(B), .out(subtractor_1_out), .bin(1'b0), .bout(subtractor_1_bout));
  assign and_1_out = A & B;  // AND_Gate and_1, 16 bits wide
  assign or_1_out = A | B;  // OR_Gate or_1, 16 bits wide
  assign xor_1_out = A ^ B;  // XOR_Gate xor_1, 16 bits wide
  Adder #(.width(16)) adder_2 (.a(A), .b({16{1'b0}}), .out(adder_2_out), .cin(1'b1), .cout(adder_2_cout));
  or or_2 (E, adder_1_cout, subtractor_1_bout, adder_2_cout);
  Multiplexer #(.select(3), .width(16)) multiplexer_1 (
    .in1(adder_1_out), .in2(subtractor_1_out), .in3(A), .in4(and_1_out), .in5(or_1_out), .in6(xor_1_out),
    .in7(adder_2_out), .out(AC_Output), .sel(ALU_Selection_Lines));  // open: in0, en
endmodule

module control_unit (
  input  [15:0] AC,
  input  [15:0] IR,
  output AR_Ld,
  output DR_Ld,
  output AC_Ld,
  output Clk,
  output PC_Inc,
  output PC_Ld,
  output IR_Ld,
  output Memory_Read_En,
  output Memory_Write_En,
  output [2:0] Bus_Selection_Lines,
  output [2:0] ALU_Selection_Lines
);

  wire and_1_out, and_2_out, and_3_out, and_4_out, and_5_out, and_6_out, and_7_out, and_8_out, and_9_out,
       and_10_out, and_11_out, and_12_out, and_13_out, and_14_out, and_15_out, and_16_out, and_17_out,
       and_18_out, and_19_out, and_21_out, and_22_out, and_23_out, and_24_out, and_26_out, and_27_out,
       and_28_out, and_29_out, and_31_out, and_32_out, and_36_out, and_37_out, and_38_out, and_39_out,
       and_40_out, and_42_out, and_43_out, D0, D1, D2, D3, D4, D5, D6, D7, d_ff_2_q, I, not_1_out, not_2_out,
       not_3_out, not_5_out, not_6_out, not_7_out, not_8_out, not_9_out, not_10_out, Sequence_Counter_CLR,
       Sequence_Counter_Inc, T0, T2, T3, T4, T5, T6, T7, T8, T9, T10, T11, T12, T13, T14, T15, X0, X1, X4,
       Y1, Y2, Y3, Y4, Y7;
  wire [3:0] Sequence_Counter_q;

  not not_1 (not_1_out, I);
  not not_2 (not_2_out, I);
  and and_1 (and_1_out, T5, D2);
  and and_2 (and_2_out, T5, D1);
  and and_3 (and_3_out, T6, D5);
  and and_4 (and_4_out, T4, D4);
  and and_5 (and_5_out, T5, D0);
  and and_6 (and_6_out, T4, D3);
  and and_7 (and_7_out, T4, not_2_out, D7, IR[5]);
  not not_3 (not_3_out, and_8_out);
  and and_8 (and_8_out, AC[0], AC[1], AC[2], AC[3], AC[4], AC[5], AC[6], AC[7], AC[8], AC[9], AC[10], AC[11], AC[12], AC[13], AC[14], AC[15]);
  and and_9 (and_9_out, not_1_out, T3, D7, not_3_out, IR[2]);
  Decoder #(.select(4), .enable("false")) decoder_1 (
    .out0(T0), .out1(IR_Ld), .out2(T2), .out3(T3), .out4(T4), .out5(T5), .out6(T6), .out7(T7), .out8(T8),
    .out9(T9), .out10(T10), .out11(T11), .out12(T12), .out13(T13), .out14(T14), .out15(T15),
    .sel(Sequence_Counter_q));
  Counter #(.width(4), .max('hf)) Sequence_Counter (
    .load(1'b0), .count(Sequence_Counter_Inc), .Q(Sequence_Counter_q), .clk(Clk), .clr(d_ff_2_q));  // open: D, carry
  Clock clock_1 (.out(Clk));
  not not_4 (Sequence_Counter_Inc, Sequence_Counter_CLR);
  Decoder #(.select(3), .enable("false")) decoder_2 (
    .out0(D0), .out1(D1), .out2(D2), .out3(D3), .out4(D4), .out5(D5), .out6(D6), .out7(D7), .sel(IR[14:12]));
  or or_1 (Sequence_Counter_CLR, and_1_out, and_2_out, and_3_out, and_9_out, and_4_out, and_5_out, and_6_out, and_7_out);
  D_Flip_Flop d_ff_1 (.D(IR[15]), .Q(I));  // open: clk, Qn, preset, en, reset
  D_Flip_Flop d_ff_2 (.clk(Clk), .D(Sequence_Counter_CLR), .Q(d_ff_2_q));  // open: Qn, preset, en, reset
  and and_10 (and_10_out, T4, D2);
  and and_11 (and_11_out, T4, D1);
  and and_12 (and_12_out, T4, D5);
  and and_13 (and_13_out, T5, D5);
  not not_5 (not_5_out, I);
  and and_14 (and_14_out, T4, D0);
  and and_15 (and_15_out, T5, D2);
  and and_16 (and_16_out, T5, D1);
  and and_17 (and_17_out, T6, D5);
  and and_18 (and_18_out, T5, D5);
  not not_6 (not_6_out, I);
  and and_19 (and_19_out, T5, D0);
  not not_7 (not_7_out, I);
  and and_20 (PC_Ld, T4, D4);
  and and_21 (and_21_out, T4, D2);
  and and_22 (and_22_out, T4, D1);
  and and_23 (and_23_out, T4, D5);
  and and_24 (and_24_out, T4, D0);
  and and_25 (Memory_Write_En, T4, D3);
  and and_26 (and_26_out, T4, D2);
  and and_27 (and_27_out, T4, D1);
  and and_28 (and_28_out, T4, D5);
  and and_29 (and_29_out, T4, D0);
  and and_30 (X1, T4, D4);
  and and_31 (and_31_out, T5, D5);
  not not_8 (not_8_out, I);
  and and_32 (and_32_out, T4, D3);
  and and_33 (Y1, T5, D1);
  and and_34 (Y2, T6, D5);
  and and_35 (Y4, T5, D0);
  not not_9 (not_9_out, I);
  and and_36 (and_36_out, T5, D5);
  and and_37 (and_37_out, T5, D2);
  or or_2 (AR_Ld, T0, T2);
  and and_38 (and_38_out, T3, not_5_out, D7, IR[5]);
  and and_39 (and_39_out, T4, not_6_out, D7, IR[5]);
  and and_40 (and_40_out, T3, not_8_out, D7, IR[5]);
  and and_41 (Y7, T4, not_9_out, D7, IR[5]);
  or or_3 (Y3, and_36_out, and_37_out);
  or or_4 (DR_Ld, and_10_out, and_11_out, and_12_out, and_13_out, and_38_out, and_14_out);
  not not_10 (not_10_out, and_42_out);
  and and_42 (and_42_out, AC[0], AC[1], AC[2], AC[3], AC[4], AC[5], AC[6], AC[7], AC[8], AC[9], AC[10], AC[11], AC[12], AC[13], AC[14], AC[15]);
  or or_5 (Memory_Read_En, IR_Ld, and_21_out, and_22_out, and_23_out, and_24_out);
  or or_6 (X0, IR_Ld, and_26_out, and_27_out, and_28_out, and_29_out);
  or or_7 (X4, and_31_out, and_40_out, and_32_out);
  or or_8 (AC_Ld, and_15_out, and_16_out, and_17_out, and_18_out, and_39_out, and_19_out);
  and and_43 (and_43_out, not_7_out, T3, D7, not_10_out, IR[2]);
  or or_9 (PC_Inc, IR_Ld, and_43_out);
  Priority_Encoder priority_encoder_1 (
    .in0(X0), .in1(X1), .in2(1'b0), .in3(1'b0), .in4(X4), .in5(T0), .in6(T2), .in7(1'b0),
    .out(Bus_Selection_Lines));  // open: en_in, gs, en_out
  Priority_Encoder priority_encoder_2 (
    .in0(1'b0), .in1(Y1), .in2(Y2), .in3(Y3), .in4(Y4), .in5(1'b0), .in6(1'b0), .in7(Y7),
    .out(ALU_Selection_Lines));  // open: en_in, gs, en_out

  // Other names for the same wires on the sheet: B0 = IR[0]; B1 = IR[1]; B2 = IR[2]; B3 = IR[3]; B4 = IR[4];
  //   B5 = IR[5]; B6 = IR[6]; B7 = IR[7]; B8 = IR[8]; B9 = IR[9]; B10 = IR[10]; B11 = IR[11]; T1 = IR_Ld; X5 = T0;
  //   X6 = T2
endmodule
